# Fritzing sketch intro_sketch (saved by Fritzing 1.0.1rc)
breadboards: 1

parts:
  D1 = Rectifier Diode [part_number=1N4001 package="300 mil [THT]"]
  L1 = Solenoid
  Q1 = Basic FET P-Channel [package="D2Pak [SMD]"]
  R1 = Resistor [tolerance=±5% resistance=220 package="2010 [SMD]"]
  L2 = Solenoid
  D2 = Rectifier Diode [part_number=1N4001 package="300 mil [THT]"]
  R2 = Resistor [tolerance=±5% resistance=220 package="2010 [SMD]"]
  Q2 = Basic FET P-Channel [package="D2Pak [SMD]"]
  MCU1 = Raspberry Pi Zero

nets:
  N1: D1.cathode, L1.pin2, R1.Pin_1, L2.pin2, D2.cathode, MCU1.pin_2, MCU1.pin_4
  N2: D1.anode, L1.pin1, Q1.drain
  N3: Q1.Gate, R1.Pin_0
  N4: Q1.source, Q2.source, MCU1.pin_6, MCU1.pin_14, MCU1.pin_16, MCU1.pin_37, MCU1.pin_39
  N5: L2.pin1, D2.anode, Q2.drain
  N6: R2.Pin_0, Q2.Gate

// code stored in the sketch: intro_code.ino
import RPi.GPIO as GPIO
import time

# Define the GPIO pin number connected to your solenoid
solenoid_pin = 4

# Set up the GPIO mode and pin
GPIO.setmode(GPIO.BCM)
GPIO.setup(solenoid_pin, GPIO.OUT)

try:
    while True:
        # Activate the solenoid (push motion)
        GPIO.output(solenoid_pin, GPIO.HIGH)
        
        # Wait for a short duration (e.g., 0.1 seconds)
        time.sleep(0.1)
        
        # Deactivate the solenoid (release motion)
        GPIO.output(solenoid_pin, GPIO.LOW)
        
        # Wait for 1 second
        time.sleep(1)

except KeyboardInterrupt:
    # If you manually stop the script with Ctrl+C, clean up the GPIO settings
    GPIO.cleanup()
